# Fritzing sketch wiring (saved by Fritzing 0.9.3b)
breadboards: 1

parts:
  Part1 = ESP-WROOM-32 [ESP-32S] Module [part_number=ESP-WROOM-32]
  Q1 = NPN-Transistor [package="SOT-23 [SMD]"]
  Q2 = NPN-Transistor [package="SOT-23 [SMD]"]
  Q3 = NPN-Transistor [package="SOT-23 [SMD]"]
  LED1 = RGB LED - (4 legs) [package="5 mm [THT]"]

nets:
  N1: Part1.GND, Q1.2, Q2.2, Q3.2
  N2: Part1.3V3, LED1.blue_cathode
  N3: Part1.IO5, Q1.0
  N4: Part1.IO18, Q2.0
  N5: Part1.IO19, Q3.0
  N6: Q1.1, LED1.green_cathode
  N7: Q2.1, LED1.common_anode
  N8: Q3.1, LED1.red_cathode

custom parts:
  ESP-WROOM-32 [ESP-32S] Module: Espressif ESP-WROOM-32 WiFi/Bluetooth LE microcontroller module also known as the Ai-Thinker ESP-32S module with similar formfactor. The ESP32 is a microcontroller chip with WiFi and BLE capabilities. The chip is developed by Espressif and is the successor to the popular ESP8266 WiFi module.
